// Logisim project Darkstar.circ as structural Verilog: 11 circuits, main circuit main
module main (
  input  Reset
);

  wire Arithmetic_Engine_c, Arithmetic_Engine_n, Arithmetic_Engine_v, Arithmetic_Engine_z, Clk_out,
       CU_auipc_flag, CU_b_src, CU_branch, CU_jal_flag, CU_jalr_flag, CU_lui_flag, CU_memread, CU_memsigned,
       CU_memwrite, CU_negate, CU_regwrite, CU_wordflag, or_1_out, or_2_out, or_3_out, PC_Adder_cout;
  wire [1:0] CU_memsize;
  wire [2:0] CU_alu_op;
  wire [11:0] multiplexer_4_out;
  wire [31:0] Arithmetic_Engine_result, Arithmetic_Engine_result_2;
  wire [63:0] bit_extender_1_out, bit_extender_2_out, bit_extender_3_out, Data_data_out, Instructions_instr,
       Internal_Registers_pc_out, Internal_Registers_reg1_out, Internal_Registers_reg2_out,
       multiplexer_1_out, multiplexer_2_out, multiplexer_3_out, multiplexer_5_out, multiplexer_6_out,
       multiplexer_7_out, multiplexer_8_out, multiplexer_9_out, multiplexer_10_out, multiplexer_11_out,
       multiplexer_12_out, multiplexer_13_out, PC_Adder_s, undriven;

  Clock Clk (.out(Clk_out));
  Multiplexer #(.width(64)) multiplexer_1 (
    .in0(64'h8), .in1(multiplexer_7_out), .out(multiplexer_1_out), .sel(or_1_out));
  or or_1 (or_1_out, CU_branch, CU_jal_flag);
  Program_Memory Instructions (.PC(Internal_Registers_pc_out), .Instr(Instructions_instr));
  CLA64 PC_Adder (.A(Internal_Registers_pc_out), .B(multiplexer_1_out), .S(PC_Adder_s), .Cout(PC_Adder_cout));
  // NoConnect on PC_Adder_cout
  assign bit_extender_1_out = {{51{Instructions_instr[31]}}, {Instructions_instr[31], Instructions_instr[7], Instructions_instr[30:25], Instructions_instr[11:8], 1'b0}};  // Bit_Extender bit_extender_1
  assign bit_extender_2_out = {{43{Instructions_instr[31]}}, {Instructions_instr[31], Instructions_instr[19:12], Instructions_instr[20], Instructions_instr[30:21], 1'b0}};  // Bit_Extender bit_extender_2
  Multiplexer #(.width(64)) multiplexer_2 (
    .in0(multiplexer_12_out), .in1(PC_Adder_s), .out(multiplexer_2_out), .sel(CU_jalr_flag));
  Multiplexer #(.width(64)) multiplexer_3 (
    .in0(PC_Adder_s), .in1({multiplexer_12_out[63:1], 1'b0}), .out(multiplexer_3_out), .sel(CU_jalr_flag));
  Control_Unit CU (
    .Op(Instructions_instr[6:0]), .funct3(Instructions_instr[14:12]), .funct7_5(Instructions_instr[30]),
    .Negative(Arithmetic_Engine_n), .Zero(Arithmetic_Engine_z), .Carry(Arithmetic_Engine_c),
    .Overflow(Arithmetic_Engine_v), .ALU_Op(CU_alu_op), .Negate(CU_negate), .RegWrite(CU_regwrite),
    .B_Src(CU_b_src), .MemSigned(CU_memsigned), .MemWrite(CU_memwrite), .MemRead(CU_memread),
    .MemSize(CU_memsize), .Branch(CU_branch), .LUI_Flag(CU_lui_flag), .AUIPC_Flag(CU_auipc_flag),
    .JAL_Flag(CU_jal_flag), .JALR_Flag(CU_jalr_flag), .WordFlag(CU_wordflag));
  Multiplexer #(.width(12)) multiplexer_4 (
    .in0(Instructions_instr[31:20]), .in1({Instructions_instr[31:25], Instructions_instr[11:7]}),
    .out(multiplexer_4_out), .sel(CU_memwrite));
  assign bit_extender_3_out = {{52{multiplexer_4_out[11]}}, multiplexer_4_out};  // Bit_Extender bit_extender_3
  or or_2 (or_2_out, CU_auipc_flag, CU_lui_flag);
  Multiplexer #(.width(64)) multiplexer_5 (
    .in0(bit_extender_3_out), .in1(bit_extender_1_out), .out(multiplexer_5_out), .sel(CU_branch));
  Regfile Internal_Registers (
    .Read_Register1(Instructions_instr[19:15]), .Read_Register2(Instructions_instr[24:20]),
    .Write_Data(multiplexer_2_out), .Clock(Clk_out), .Reset(Reset),
    .Write_Register(Instructions_instr[11:7]), .Write_Enable(CU_regwrite), .PC_In(multiplexer_3_out),
    .Reg1_Out(Internal_Registers_reg1_out), .Reg2_Out(Internal_Registers_reg2_out),
    .PC_Out(Internal_Registers_pc_out));
  Multiplexer #(.width(64)) multiplexer_6 (
    .in0(multiplexer_5_out), .in1({undriven[63:32], Instructions_instr[31:12], {11{1'b0}}, undriven[0]}),
    .out(multiplexer_6_out), .sel(or_2_out));
  Multiplexer #(.width(64)) multiplexer_7 (
    .in0(multiplexer_6_out), .in1(bit_extender_2_out), .out(multiplexer_7_out), .sel(CU_jal_flag));
  Multiplexer #(.width(64)) multiplexer_8 (
    .in0(Internal_Registers_reg2_out), .in1(multiplexer_7_out), .out(multiplexer_8_out), .sel(CU_b_src));
  or or_3 (or_3_out, CU_auipc_flag, CU_jal_flag);
  Multiplexer #(.width(64)) multiplexer_9 (
    .in0(Internal_Registers_reg1_out), .in1({64{1'b0}}), .out(multiplexer_9_out), .sel(CU_lui_flag));
  Multiplexer #(.width(64)) multiplexer_10 (
    .in0(multiplexer_8_out), .in1(64'h8), .out(multiplexer_10_out), .sel(CU_jal_flag));
  Multiplexer #(.width(64)) multiplexer_11 (
    .in0(multiplexer_9_out), .in1(Internal_Registers_pc_out), .out(multiplexer_11_out), .sel(or_3_out));
  Multiplexer #(.width(64)) multiplexer_12 (
    .in0(multiplexer_13_out), .in1(Data_data_out), .out(multiplexer_12_out), .sel(CU_memread));
  Multiplexer #(.width(64)) multiplexer_13 (
    .in0({Arithmetic_Engine_result_2, Arithmetic_Engine_result}),
    .in1({{32{1'b0}}, Arithmetic_Engine_result}), .out(multiplexer_13_out), .sel(CU_wordflag));
  ALU Arithmetic_Engine (
    .A(multiplexer_11_out), .B(multiplexer_10_out), .ALU_Op(CU_alu_op), .Negate(CU_negate),
    .Result({Arithmetic_Engine_result_2, Arithmetic_Engine_result}), .N(Arithmetic_Engine_n),
    .Z(Arithmetic_Engine_z), .C(Arithmetic_Engine_c), .V(Arithmetic_Engine_v));
  Data_Memory Data (
    .Reset(Reset), .Unsigned0_Signed1(CU_memsigned),
    .Address({Arithmetic_Engine_result_2, Arithmetic_Engine_result}), .Store(CU_memwrite), .Load(CU_memread),
    .Clock(Clk_out), .Data_In(Internal_Registers_reg2_out), .Size_Flag(CU_memsize), .Data_Out(Data_data_out));
endmodule

module Control_Unit (
  input  [6:0] Op,
  input  [2:0] funct3,
  input  funct7_5,
  input  Negative,
  input  Zero,
  input  Carry,
  input  Overflow,
  output [2:0] ALU_Op,
  output Negate,
  output RegWrite,
  output B_Src,
  output MemSigned,
  output MemWrite,
  output MemRead,
  output [1:0] MemSize,
  output Branch,
  output LUI_Flag,
  output AUIPC_Flag,
  output JAL_Flag,
  output JALR_Flag,
  output WordFlag
);

  wire and_1_out, and_2_out, and_3_out, B_Type_out, BEQ_out, BGE_out, BGEU_out, BLT_out, BLTU_out, BNE_out,
       decoder_1_out0, decoder_1_out1, decoder_1_out2, decoder_1_out3, decoder_1_out4, decoder_1_out5,
       decoder_1_out6, decoder_1_out7, I_Type_out, LB_out, LBU_out, LH_out, LHU_out, LW_out, not_1_out,
       not_2_out, not_3_out, not_4_out, not_5_out, not_6_out, not_7_out, not_8_out, not_9_out, not_10_out,
       not_11_out, not_12_out, not_13_out, not_14_out, not_15_out, not_16_out, not_17_out, not_18_out,
       not_19_out, not_20_out, not_21_out, not_22_out, not_23_out, not_24_out, not_25_out, not_26_out,
       not_27_out, not_28_out, not_29_out, not_30_out, or_1_out, or_2_out, or_3_out, or_7_out, or_8_out,
       R_Type_out, SB_out, SH_out, SW_out, xor_1_out;

  Decoder #(.enable("false"), .select(3)) decoder_1 (
    .out0(decoder_1_out0), .out1(decoder_1_out1), .out2(decoder_1_out2), .out3(decoder_1_out3),
    .out4(decoder_1_out4), .out5(decoder_1_out5), .out6(decoder_1_out6), .out7(decoder_1_out7), .sel(funct3));
  not not_1 (not_1_out, Op[6]);
  not not_2 (not_2_out, Op[5]);
  not not_3 (not_3_out, Op[3]);
  not not_4 (not_4_out, Op[2]);
  not not_5 (not_5_out, Op[6]);
  not not_6 (not_6_out, Op[3]);
  not not_7 (not_7_out, Op[2]);
  not not_8 (not_8_out, Op[4]);
  not not_9 (not_9_out, Op[3]);
  not not_10 (not_10_out, Op[2]);
  not not_11 (not_11_out, Op[6]);
  not not_12 (not_12_out, Op[3]);
  not not_13 (not_13_out, Op[6]);
  not not_14 (not_14_out, Op[5]);
  not not_15 (not_15_out, Op[3]);
  not not_16 (not_16_out, Op[4]);
  not not_17 (not_17_out, Op[4]);
  not not_18 (not_18_out, Op[3]);
  not not_19 (not_19_out, Op[6]);
  not not_20 (not_20_out, Op[5]);
  not not_21 (not_21_out, Op[4]);
  not not_22 (not_22_out, Op[3]);
  not not_23 (not_23_out, Op[2]);
  not not_24 (not_24_out, Op[6]);
  not not_25 (not_25_out, Op[4]);
  not not_26 (not_26_out, Op[3]);
  not not_27 (not_27_out, Op[2]);
  xor xor_1 (xor_1_out, Negative, Overflow);
  and I_Type (I_Type_out, not_1_out, not_2_out, Op[4], not_3_out, not_4_out, Op[1], Op[0]);
  and R_Type (R_Type_out, not_5_out, Op[5], Op[4], not_6_out, not_7_out, Op[1], Op[0]);
  and B_Type (B_Type_out, Op[6], Op[5], not_8_out, not_9_out, not_10_out, Op[1], Op[0]);
  and LUI (LUI_Flag, not_11_out, Op[5], Op[4], not_12_out, Op[2], Op[1], Op[0]);
  and AUIPC (AUIPC_Flag, not_13_out, not_14_out, Op[4], not_15_out, Op[2], Op[1], Op[0]);
  and JAL (JAL_Flag, Op[6], Op[5], not_16_out, Op[3], Op[2], Op[1], Op[0]);
  and JALR (JALR_Flag, Op[6], Op[5], not_17_out, not_18_out, Op[2], Op[1], Op[0]);
  and LOAD (MemRead, not_19_out, not_20_out, not_21_out, not_22_out, not_23_out, Op[1], Op[0]);
  and STORE (MemWrite, not_24_out, Op[5], not_25_out, not_26_out, not_27_out, Op[1], Op[0]);
  or or_1 (or_1_out, I_Type_out, R_Type_out);
  or or_2 (or_2_out, decoder_1_out2, decoder_1_out3);
  Multiplexer #(.width(3)) multiplexer_1 (.in0(3'b000), .in1(funct3), .out(ALU_Op), .sel(or_1_out));
  and and_1 (and_1_out, or_2_out, or_3_out);
  or or_3 (or_3_out, I_Type_out, R_Type_out);
  and and_2 (and_2_out, R_Type_out, decoder_1_out0, funct7_5);
  and and_3 (and_3_out, or_3_out, funct7_5, decoder_1_out5);
  not not_28 (not_28_out, Zero);
  not not_29 (not_29_out, xor_1_out);
  not not_30 (not_30_out, Carry);
  or or_4 (RegWrite, I_Type_out, R_Type_out, LUI_Flag, AUIPC_Flag, JAL_Flag, JALR_Flag, MemRead);
  or or_5 (B_Src, MemRead, JALR_Flag, MemWrite, JAL_Flag, AUIPC_Flag, I_Type_out, LUI_Flag);
  and LB (LB_out, MemRead, decoder_1_out0);
  and LH (LH_out, MemRead, decoder_1_out1);
  and LW (LW_out, MemRead, decoder_1_out2);
  and LBU (LBU_out, MemRead, decoder_1_out4);
  and LHU (LHU_out, MemRead, decoder_1_out5);
  and SB (SB_out, MemWrite, decoder_1_out0);
  and SH (SH_out, MemWrite, decoder_1_out1);
  and SW (SW_out, MemWrite, decoder_1_out2);
  and BEQ (BEQ_out, B_Type_out, decoder_1_out0, Zero);
  and BNE (BNE_out, B_Type_out, decoder_1_out1, not_28_out);
  and BLT (BLT_out, B_Type_out, decoder_1_out4, xor_1_out);
  and BGE (BGE_out, B_Type_out, decoder_1_out5, not_29_out);
  and BLTU (BLTU_out, B_Type_out, decoder_1_out6, not_30_out);
  and BGEU (BGEU_out, B_Type_out, decoder_1_out7, Carry);
  or or_6 (Negate, B_Type_out, and_1_out, and_2_out, and_3_out);
  or or_7 (or_7_out, LB_out, LBU_out, LH_out, LHU_out, SB_out, SH_out);
  or or_8 (or_8_out, LB_out, LBU_out, LW_out, SB_out, SW_out);
  or or_9 (MemSigned, LH_out, LB_out);
  not not_31 (MemSize[1], or_7_out);
  not not_32 (MemSize[0], or_8_out);
  or or_10 (Branch, BEQ_out, BNE_out, BLT_out, BGE_out, BLTU_out, BGEU_out);
endmodule

module Regfile (
  input  [4:0] Read_Register1,
  input  [4:0] Read_Register2,
  input  [63:0] Write_Data,
  input  Clock,
  input  Reset,
  input  [4:0] Write_Register,
  input  Write_Enable,
  input  [63:0] PC_In,
  output [63:0] Reg1_Out,
  output [63:0] Reg2_Out,
  output [63:0] PC_Out
);

  wire decoder_1_out1, decoder_1_out2, decoder_1_out3, decoder_1_out4, decoder_1_out5, decoder_1_out6,
       decoder_1_out7, decoder_1_out8, decoder_1_out9, decoder_1_out10, decoder_1_out11, decoder_1_out12,
       decoder_1_out13, decoder_1_out14, decoder_1_out15, decoder_1_out16, decoder_1_out17, decoder_1_out18,
       decoder_1_out19, decoder_1_out20, decoder_1_out21, decoder_1_out22, decoder_1_out23, decoder_1_out24,
       decoder_1_out25, decoder_1_out26, decoder_1_out27, decoder_1_out28, decoder_1_out29, decoder_1_out30,
       decoder_1_out31;
  wire [63:0] x0_q, x1_q, x2_q, x3_q, x4_q, x5_q, x6_q, x7_q, x8_q, x9_q, x10_q, x11_q, x12_q, x13_q, x14_q,
       x15_q, x16_q, x17_q, x18_q, x19_q, x20_q, x21_q, x22_q, x23_q, x24_q, x25_q, x26_q, x27_q, x28_q,
       x29_q, x30_q, x31_q;

  Decoder #(.select(5)) decoder_1 (
    .out1(decoder_1_out1), .out2(decoder_1_out2), .out3(decoder_1_out3), .out4(decoder_1_out4),
    .out5(decoder_1_out5), .out6(decoder_1_out6), .out7(decoder_1_out7), .out8(decoder_1_out8),
    .out9(decoder_1_out9), .out10(decoder_1_out10), .out11(decoder_1_out11), .out12(decoder_1_out12),
    .out13(decoder_1_out13), .out14(decoder_1_out14), .out15(decoder_1_out15), .out16(decoder_1_out16),
    .out17(decoder_1_out17), .out18(decoder_1_out18), .out19(decoder_1_out19), .out20(decoder_1_out20),
    .out21(decoder_1_out21), .out22(decoder_1_out22), .out23(decoder_1_out23), .out24(decoder_1_out24),
    .out25(decoder_1_out25), .out26(decoder_1_out26), .out27(decoder_1_out27), .out28(decoder_1_out28),
    .out29(decoder_1_out29), .out30(decoder_1_out30), .out31(decoder_1_out31), .sel(Write_Register),
    .en(Write_Enable));  // open: out0
  Register #(.width(64)) x0 (.en(1'b0), .clk(Clock), .Q(x0_q), .clr(Reset));  // open: D
  Register #(.width(64)) x1 (.D(Write_Data), .en(decoder_1_out1), .clk(Clock), .Q(x1_q), .clr(Reset));
  Register #(.width(64)) x2 (.D(Write_Data), .en(decoder_1_out2), .clk(Clock), .Q(x2_q), .clr(Reset));
  Register #(.width(64)) x3 (.D(Write_Data), .en(decoder_1_out3), .clk(Clock), .Q(x3_q), .clr(Reset));
  Register #(.width(64)) x4 (.D(Write_Data), .en(decoder_1_out4), .clk(Clock), .Q(x4_q), .clr(Reset));
  Register #(.width(64)) x5 (.D(Write_Data), .en(decoder_1_out5), .clk(Clock), .Q(x5_q), .clr(Reset));
  Register #(.width(64)) x6 (.D(Write_Data), .en(decoder_1_out6), .clk(Clock), .Q(x6_q), .clr(Reset));
  Register #(.width(64)) x7 (.D(Write_Data), .en(decoder_1_out7), .clk(Clock), .Q(x7_q), .clr(Reset));
  Register #(.width(64)) x8 (.D(Write_Data), .en(decoder_1_out8), .clk(Clock), .Q(x8_q), .clr(Reset));
  Register #(.width(64)) x9 (.D(Write_Data), .en(decoder_1_out9), .clk(Clock), .Q(x9_q), .clr(Reset));
  Register #(.width(64)) x10 (.D(Write_Data), .en(decoder_1_out10), .clk(Clock), .Q(x10_q), .clr(Reset));
  Register #(.width(64)) x11 (.D(Write_Data), .en(decoder_1_out11), .clk(Clock), .Q(x11_q), .clr(Reset));
  Register #(.width(64)) x12 (.D(Write_Data), .en(decoder_1_out12), .clk(Clock), .Q(x12_q), .clr(Reset));
  Register #(.width(64)) x13 (.D(Write_Data), .en(decoder_1_out13), .clk(Clock), .Q(x13_q), .clr(Reset));
  Register #(.width(64)) x14 (.D(Write_Data), .en(decoder_1_out14), .clk(Clock), .Q(x14_q), .clr(Reset));
  Register #(.width(64)) x15 (.D(Write_Data), .en(decoder_1_out15), .clk(Clock), .Q(x15_q), .clr(Reset));
  Register #(.width(64)) x16 (.D(Write_Data), .en(decoder_1_out16), .clk(Clock), .Q(x16_q), .clr(Reset));
  Register #(.width(64)) x17 (.D(Write_Data), .en(decoder_1_out17), .clk(Clock), .Q(x17_q), .clr(Reset));
  Register #(.width(64)) x18 (.D(Write_Data), .en(decoder_1_out18), .clk(Clock), .Q(x18_q), .clr(Reset));
  Register #(.width(64)) x19 (.D(Write_Data), .en(decoder_1_out19), .clk(Clock), .Q(x19_q), .clr(Reset));
  Register #(.width(64)) x20 (.D(Write_Data), .en(decoder_1_out20), .clk(Clock), .Q(x20_q), .clr(Reset));
  Register #(.width(64)) x21 (.D(Write_Data), .en(decoder_1_out21), .clk(Clock), .Q(x21_q), .clr(Reset));
  Register #(.width(64)) x22 (.D(Write_Data), .en(decoder_1_out22), .clk(Clock), .Q(x22_q), .clr(Reset));
  Register #(.width(64)) x23 (.D(Write_Data), .en(decoder_1_out23), .clk(Clock), .Q(x23_q), .clr(Reset));
  Register #(.width(64)) x24 (.D(Write_Data), .en(decoder_1_out24), .clk(Clock), .Q(x24_q), .clr(Reset));
  Register #(.width(64)) x25 (.D(Write_Data), .en(decoder_1_out25), .clk(Clock), .Q(x25_q), .clr(Reset));
  Register #(.width(64)) x26 (.D(Write_Data), .en(decoder_1_out26), .clk(Clock), .Q(x26_q), .clr(Reset));
  Register #(.width(64)) x27 (.D(Write_Data), .en(decoder_1_out27), .clk(Clock), .Q(x27_q), .clr(Reset));
  Register #(.width(64)) x28 (.D(Write_Data), .en(decoder_1_out28), .clk(Clock), .Q(x28_q), .clr(Reset));
  Register #(.width(64)) x29 (.D(Write_Data), .en(decoder_1_out29), .clk(Clock), .Q(x29_q), .clr(Reset));
  Register #(.width(64)) x30 (.D(Write_Data), .en(decoder_1_out30), .clk(Clock), .Q(x30_q), .clr(Reset));
  Register #(.width(64)) x31 (.D(Write_Data), .en(decoder_1_out31), .clk(Clock), .Q(x31_q), .clr(Reset));
  Register #(.width(64)) pc (.D(PC_In), .en(1'b1), .clk(Clock), .Q(PC_Out), .clr(Reset));
  Multiplexer #(.select(5), .width(64)) multiplexer_1 (
    .in0(x0_q), .in1(x1_q), .in2(x2_q), .in3(x3_q), .in4(x4_q), .in5(x5_q), .in6(x6_q), .in7(x7_q),
    .in8(x8_q), .in9(x9_q), .in10(x10_q), .in11(x11_q), .in12(x12_q), .in13(x13_q), .in14(x14_q),
    .in15(x15_q), .in16(x16_q), .in17(x17_q), .in18(x18_q), .in19(x19_q), .in20(x20_q), .in21(x21_q),
    .in22(x22_q), .in23(x23_q), .in24(x24_q), .in25(x25_q), .in26(x26_q), .in27(x27_q), .in28(x28_q),
    .in29(x29_q), .in30(x30_q), .in31(x31_q), .out(Reg1_Out), .sel(Read_Register1));
  Multiplexer #(.select(5), .width(64)) multiplexer_2 (
    .in0(x0_q), .in1(x1_q), .in2(x2_q), .in3(x3_q), .in4(x4_q), .in5(x5_q), .in6(x6_q), .in7(x7_q),
    .in8(x8_q), .in9(x9_q), .in10(x10_q), .in11(x11_q), .in12(x12_q), .in13(x13_q), .in14(x14_q),
    .in15(x15_q), .in16(x16_q), .in17(x17_q), .in18(x18_q), .in19(x19_q), .in20(x20_q), .in21(x21_q),
    .in22(x22_q), .in23(x23_q), .in24(x24_q), .in25(x25_q), .in26(x26_q), .in27(x27_q), .in28(x28_q),
    .in29(x29_q), .in30(x30_q), .in31(x31_q), .out(Reg2_Out), .sel(Read_Register2));
endmodule

module ALU (
  input  [63:0] A,
  input  [63:0] B,
  input  [2:0] ALU_Op,
  input  Negate,
  output [63:0] Result,
  output N,
  output Z,
  output C,
  output V
);

  wire ALU_Adder_cout, and_2_out, and_3_out, nor_1_out, not_1_out, not_2_out, or_2_out, xnor_1_out,
       xor_1_out, xor_3_out, xor_4_out;
  wire [63:0] ALU_Adder_s, and_1_out, bit_extender_1_out, bit_extender_2_out, multiplexer_1_out,
       multiplexer_2_out, negator_1_out, or_1_out, shifter_1_out, shifter_2_out, shifter_3_out, xor_2_out;

  Negator #(.width(64)) negator_1 (.in(B), .out(negator_1_out));
  Multiplexer #(.width(64)) multiplexer_1 (.in0(B), .in1(negator_1_out), .out(multiplexer_1_out), .sel(Negate));
  xor xor_1 (xor_1_out, ALU_Adder_s[63], V);
  not not_1 (not_1_out, ALU_Adder_cout);
  assign bit_extender_1_out = {{63{1'b0}}, xor_1_out};  // Bit_Extender bit_extender_1
  assign bit_extender_2_out = {{63{1'b0}}, not_1_out};  // Bit_Extender bit_extender_2
  Shifter #(.width(64)) shifter_1 (.in(A), .\dist (B[5:0]), .out(shifter_1_out));
  assign xor_2_out = A ^ B;  // XOR_Gate xor_2, 64 bits wide
  Shifter #(.shift("lr"), .width(64)) shifter_2 (.in(A), .\dist (B[5:0]), .out(shifter_2_out));
  Shifter #(.shift("ar"), .width(64)) shifter_3 (.in(A), .\dist (B[5:0]), .out(shifter_3_out));
  assign or_1_out = A | B;  // OR_Gate or_1, 64 bits wide
  assign and_1_out = A & B;  // AND_Gate and_1, 64 bits wide
  CLA64 ALU_Adder (.A(A), .B(multiplexer_1_out), .S(ALU_Adder_s), .Cout(ALU_Adder_cout));
  Multiplexer #(.width(64)) multiplexer_2 (
    .in0(shifter_2_out), .in1(shifter_3_out), .out(multiplexer_2_out), .sel(Negate));
  Multiplexer #(.select(3), .width(64)) multiplexer_3 (
    .in0(ALU_Adder_s), .in1(shifter_1_out), .in2(bit_extender_1_out), .in3(bit_extender_2_out),
    .in4(xor_2_out), .in5(multiplexer_2_out), .in6(or_1_out), .in7(and_1_out), .out({N, Result[62:0]}),
    .sel(ALU_Op));
  not not_2 (not_2_out, Negate);
  nor nor_1 (nor_1_out, ALU_Op[0], ALU_Op[1], ALU_Op[2]);
  xor xor_3 (xor_3_out, ALU_Adder_s[63], A[63]);
  xnor xnor_1 (xnor_1_out, A[63], B[63]);
  xor xor_4 (xor_4_out, A[63], B[63]);
  and and_2 (and_2_out, xnor_1_out, not_2_out);
  and and_3 (and_3_out, xor_4_out, Negate);
  and and_4 (C, nor_1_out, ALU_Adder_cout);
  or or_2 (or_2_out, and_2_out, and_3_out);
  and and_5 (V, xor_3_out, or_2_out);
  nor nor_2 (Z, Result[0], Result[1], Result[2], Result[3], Result[4], Result[5], Result[6], Result[7], Result[8], Result[9], Result[10], Result[11], Result[12], Result[13], Result[14], Result[15], Result[16], Result[17], Result[18], Result[19], Result[20], Result[21], Result[22], Result[23], Result[24], Result[25], Result[26], Result[27], Result[28], Result[29], Result[30], Result[31], Result[32], Result[33], Result[34], Result[35], Result[36], Result[37], Result[38], Result[39], Result[40], Result[41], Result[42], Result[43], Result[44], Result[45], Result[46], Result[47], Result[48], Result[49], Result[50], Result[51], Result[52], Result[53], Result[54], Result[55], Result[56], Result[57], Result[58], Result[59], Result[60], Result[61], Result[62], N);

  assign Result[63] = N;

  // Notes on the sheet:
  //   ALU Opcodes
  //   000 = ADD/SUB
  //   001 = SLL
  //   010 = SLT
  //   011 = SLTU
  //   100 = XOR
  //   101 = SRL/SRA
  //   110 = OR
  //   111 = AND
  //   Negate determines whether to use B or -B or to use SRL/SRA
  //   Negate = funct7[5]
  //   Flags
endmodule

module CLA64 (
  input  [63:0] A,
  input  [63:0] B,
  output [63:0] S,
  output Cout
);

  wire CLA4_0_cout, CLA4_1_cout, CLA4_2_cout, CLA4_3_cout, CLA4_4_cout, CLA4_5_cout, CLA4_6_cout,
       CLA4_7_cout, CLA4_8_cout, CLA4_9_cout, CLA4_10_cout, CLA4_11_cout, CLA4_12_cout, CLA4_13_cout,
       CLA4_14_cout;

  CLA4 CLA4_0 (.A(A[3:0]), .B(B[3:0]), .Cin(1'b0), .S(S[3:0]), .Cout(CLA4_0_cout));
  CLA4 CLA4_1 (.A(A[7:4]), .B(B[7:4]), .Cin(CLA4_0_cout), .S(S[7:4]), .Cout(CLA4_1_cout));
  CLA4 CLA4_2 (.A(A[11:8]), .B(B[11:8]), .Cin(CLA4_1_cout), .S(S[11:8]), .Cout(CLA4_2_cout));
  CLA4 CLA4_3 (.A(A[15:12]), .B(B[15:12]), .Cin(CLA4_2_cout), .S(S[15:12]), .Cout(CLA4_3_cout));
  CLA4 CLA4_4 (.A(A[19:16]), .B(B[19:16]), .Cin(CLA4_3_cout), .S(S[19:16]), .Cout(CLA4_4_cout));
  CLA4 CLA4_5 (.A(A[23:20]), .B(B[23:20]), .Cin(CLA4_4_cout), .S(S[23:20]), .Cout(CLA4_5_cout));
  CLA4 CLA4_6 (.A(A[27:24]), .B(B[27:24]), .Cin(CLA4_5_cout), .S(S[27:24]), .Cout(CLA4_6_cout));
  CLA4 CLA4_7 (.A(A[31:28]), .B(B[31:28]), .Cin(CLA4_6_cout), .S(S[31:28]), .Cout(CLA4_7_cout));
  CLA4 CLA4_8 (.A(A[35:32]), .B(B[35:32]), .Cin(CLA4_7_cout), .S(S[35:32]), .Cout(CLA4_8_cout));
  CLA4 CLA4_9 (.A(A[39:36]), .B(B[39:36]), .Cin(CLA4_8_cout), .S(S[39:36]), .Cout(CLA4_9_cout));
  CLA4 CLA4_10 (.A(A[43:40]), .B(B[43:40]), .Cin(CLA4_9_cout), .S(S[43:40]), .Cout(CLA4_10_cout));
  CLA4 CLA4_11 (.A(A[47:44]), .B(B[47:44]), .Cin(CLA4_10_cout), .S(S[47:44]), .Cout(CLA4_11_cout));
  CLA4 CLA4_12 (.A(A[51:48]), .B(B[51:48]), .Cin(CLA4_11_cout), .S(S[51:48]), .Cout(CLA4_12_cout));
  CLA4 CLA4_13 (.A(A[55:52]), .B(B[55:52]), .Cin(CLA4_12_cout), .S(S[55:52]), .Cout(CLA4_13_cout));
  CLA4 CLA4_14 (.A(A[59:56]), .B(B[59:56]), .Cin(CLA4_13_cout), .S(S[59:56]), .Cout(CLA4_14_cout));
  CLA4 CLA4_15 (.A(A[63:60]), .B(B[63:60]), .Cin(CLA4_14_cout), .S(S[63:60]), .Cout(Cout));
endmodule

module CLA4 (
  input  [3:0] A,
  input  [3:0] B,
  input  Cin,
  output [3:0] S,
  output Cout
);

  wire and_1_out, and_2_out, and_3_out, and_4_out, and_5_out, and_6_out, and_7_out, and_8_out, and_9_out,
       and_10_out, and_11_out, and_12_out, and_13_out, and_14_out, and_15_out, and_16_out, and_17_out,
       and_18_out, and_19_out, and_20_out, FA0_cout, FA1_cout, FA2_cout, FA3_cout, or_1_out, or_2_out,
       or_3_out, or_4_out, or_5_out, or_6_out, or_7_out, or_8_out, or_9_out, xor_1_out, xor_2_out, xor_3_out,
       xor_4_out, xor_5_out, xor_6_out, xor_7_out, xor_8_out, xor_9_out, xor_10_out;

  and and_1 (and_1_out, A[0], B[0]);
  xor xor_1 (xor_1_out, A[0], B[0]);
  and and_2 (and_2_out, A[1], B[1]);
  xor xor_2 (xor_2_out, A[1], B[1]);
  and and_3 (and_3_out, A[0], B[0]);
  xor xor_3 (xor_3_out, A[0], B[0]);
  and and_4 (and_4_out, A[2], B[2]);
  xor xor_4 (xor_4_out, A[2], B[2]);
  and and_5 (and_5_out, A[1], B[1]);
  xor xor_5 (xor_5_out, A[1], B[1]);
  and and_6 (and_6_out, A[0], B[0]);
  xor xor_6 (xor_6_out, A[0], B[0]);
  and and_7 (and_7_out, A[3], B[3]);
  xor xor_7 (xor_7_out, A[3], B[3]);
  and and_8 (and_8_out, A[2], B[2]);
  xor xor_8 (xor_8_out, A[2], B[2]);
  and and_9 (and_9_out, A[1], B[1]);
  xor xor_9 (xor_9_out, A[1], B[1]);
  and and_10 (and_10_out, A[0], B[0]);
  xor xor_10 (xor_10_out, A[0], B[0]);
  and and_11 (and_11_out, xor_1_out, Cin);
  and and_12 (and_12_out, xor_3_out, Cin);
  and and_13 (and_13_out, xor_6_out, Cin);
  and and_14 (and_14_out, xor_10_out, Cin);
  or or_1 (or_1_out, and_1_out, and_11_out);
  or or_2 (or_2_out, and_3_out, and_12_out);
  or or_3 (or_3_out, and_6_out, and_13_out);
  or or_4 (or_4_out, and_10_out, and_14_out);
  and and_15 (and_15_out, xor_2_out, or_2_out);
  and and_16 (and_16_out, xor_5_out, or_3_out);
  and and_17 (and_17_out, xor_9_out, or_4_out);
  or or_5 (or_5_out, and_2_out, and_15_out);
  or or_6 (or_6_out, and_5_out, and_16_out);
  or or_7 (or_7_out, and_9_out, and_17_out);
  and and_18 (and_18_out, xor_4_out, or_6_out);
  and and_19 (and_19_out, xor_8_out, or_7_out);
  or or_8 (or_8_out, and_4_out, and_18_out);
  or or_9 (or_9_out, and_8_out, and_19_out);
  and and_20 (and_20_out, xor_7_out, or_9_out);
  or or_10 (Cout, and_7_out, and_20_out);
  Full_Adder FA0 (.A(A[0]), .B(B[0]), .Cin(Cin), .S(S[0]), .Cout(FA0_cout));
  // NoConnect on FA0_cout
  Full_Adder FA1 (.A(A[1]), .B(B[1]), .Cin(or_1_out), .S(S[1]), .Cout(FA1_cout));
  // NoConnect on FA1_cout
  Full_Adder FA2 (.A(A[2]), .B(B[2]), .Cin(or_5_out), .S(S[2]), .Cout(FA2_cout));
  // NoConnect on FA2_cout
  Full_Adder FA3 (.A(A[3]), .B(B[3]), .Cin(or_8_out), .S(S[3]), .Cout(FA3_cout));
  // NoConnect on FA3_cout

  // Notes on the sheet:
  //   C0 -->
  //   G0
  //   P0
  //   C0
  //   G1
  //   P0
  //   C0
  //   P0
  //   C0
  //   G2
  //   G1
  //   P0
  //   C0
  //   P1
  //   G0
  //   G2
  //   P2
  //   G1
  //   P1
  //   G0
  //   G3
  //   P3
  //   P2
  //   P1
  //   G0
  //   C1
  //   C1
  //   C1
  //   C0 = Cin
  //   C2
  //   C2
  //   C1 = G0 ∨ (P0 ∧ C0) = (A0 ∧ B0) ∨ ((A0 ⊕ B0) ∧ Cin)
  //   C2 = G1 ∨ (P1 ∧ C1) = (A1 ∧ B1) ∨ ((A1 ⊕ B1) ∧ ((A0 ∧ B0) ∨ ((A0 ⊕ B0) ∧ Cin)))
  //   C3
  //   C3 = G2 ∨ (P2 ∧ C2) = (A2 ∧ B2) ∨ ((A2 ⊕ B2) ∧ (A1 ∧ B1) ∨ ((A1 ⊕ B1) ∧ ((A0 ∧ B0) ∨ ((A0 ⊕ B0) ∧ Cin))))
  //   C1
  //   C2
  //   C3
  //   C4
  //   C4 = G3 ∨ (P3 ∧ C3) = (A3 ∧ B3) ∨ ((A3 ⊕ B3) ∧ ((A2 ∧ B2) ∨ ((A2 ⊕ B2) ∧ (A1 ∧ B1) ∨ ((A1 ⊕ B1) ∧ ((A0 ∧ B0) ∨ ((A0 ⊕ B0) ∧ Cin))))))
endmodule

module Full_Adder (
  input  A,
  input  B,
  input  Cin,
  output S,
  output Cout
);

  wire half_adder_1_c, half_adder_1_s, half_adder_2_c;

  Half_Adder half_adder_1 (.A(A), .B(B), .S(half_adder_1_s), .C(half_adder_1_c));
  Half_Adder half_adder_2 (.A(half_adder_1_s), .B(Cin), .S(S), .C(half_adder_2_c));
  or or_1 (Cout, half_adder_2_c, half_adder_1_c);
endmodule

module Half_Adder (
  input  A,
  input  B,
  output S,
  output C
);

  xor xor_1 (S, A, B);
  and and_1 (C, B, A);
endmodule

module Program_Memory (
  input  [63:0] PC,
  output [63:0] Instr
);

  // ROM #(.addrWidth(16), .line("octo")) Instruction_Memory: pin names not known; wires that end beside it: PC[15:0], Instr[7:0], Instr[15:8], Instr[23:16], Instr[31:24], Instr[39:32], Instr[47:40], Instr[55:48], Instr[63:56]

  // Notes on the sheet:
  //   contents of Instruction_Memory (hex, n*v repeats v):
  //   6f 0 0 18 44*0 b7 a2 9f 59 93 82 72 2b 67 83 6*0 b7 c2 ad de 93 82 f2 ee 13 3 10 11 b3 83 62 0 b3 83
  //   63 40 93 2 10 0 13 3 90 1 b3 93 62 0 b7 c2 ad de 93 82 f2 ee 13 3 40 6 b3 a3 62 0 b3 b3 62 0 13 3 f0
  //   ff b3 c3 62 0 b3 f2 72 0 13 3 c0 3c b3 e2 63 0 b7 2 0 80 13 3 10 1 b3 d3 62 0 b3 d3 62 40 e7 89 6*0
  //   13 e 20 3 13 e 4e fc 93 e 10 0 93 9e e 1 13 f 80 c1 93 2f 8f 3e 93 3f 8f 3e 93 4f fe ff 37 e 0 80 93
  //   5e fe 1 93 5e fe 41 37 5f 34 12 13 6e 8f 67 93 7e de 5a 67 80 6*0 93 2 d0 4 23 0 50 0 13 3 90 fa a3
  //   0 60 0 93 92 82 0 93 e2 12 f 23 11 50 0 93 92 2 1 93 e2 a2 3f 23 22 50 0 3 e 0 0 3 e 10 0 83 4e 10 0
  //   3 1f 20 0 3 5f 20 0 3 2e 40 0 67 80 14*0 93 2 f0 ff 13 3 a0 0 93 82 12 0 e3 8e 2 fe e3 9c 62 fe 13 3
  //   a3 0 93 82 12 0 e3 ce 62 fe 13 3 63 ff 93 82 f2 ff e3 de 62 fe 93 2 50 0 13 3 b0 ff 93 82 f2 ff e3
  //   ee 62 fe 93 2 b0 ff 13 3 50 0 93 82 12 0 e3 fe 62 fe 67 80 0 0 ef f0 1f eb ef f0 df eb ef f0 9f f1
  //   ef f0 5f f5 ef f0 1f fa 93 0 f0 ff 17 91 6 0 13 0 0 0 e3 e 0 fe
  //   16 MB of Program Memory
endmodule

module Data_Memory (
  input  Reset,
  input  Unsigned0_Signed1,
  input  [63:0] Address,
  input  Store,
  input  Load,
  input  Clock,
  input  [63:0] Data_In,
  input  [1:0] Size_Flag,
  output [63:0] Data_Out
);

  wire decoder_1_out0, decoder_1_out1, decoder_1_out2, decoder_1_out3, decoder_1_out4, decoder_1_out5,
       decoder_1_out6, decoder_1_out7, decoder_1_out8, decoder_1_out9, decoder_1_out10, decoder_1_out11,
       decoder_1_out12, decoder_1_out13, decoder_1_out14, decoder_1_out15, or_1_out;
  wire [63:0] RAM0_data_out, RAM1_data_out, RAM2_data_out, RAM3_data_out, RAM4_data_out, RAM5_data_out,
       RAM6_data_out, RAM7_data_out, RAM8_data_out, RAM9_data_out, RAM10_data_out, RAM11_data_out,
       RAM12_data_out, RAM13_data_out, RAM14_data_out, RAM15_data_out;

  or or_1 (or_1_out, Store, Load);
  Decoder #(.select(4)) decoder_1 (
    .out0(decoder_1_out0), .out1(decoder_1_out1), .out2(decoder_1_out2), .out3(decoder_1_out3),
    .out4(decoder_1_out4), .out5(decoder_1_out5), .out6(decoder_1_out6), .out7(decoder_1_out7),
    .out8(decoder_1_out8), .out9(decoder_1_out9), .out10(decoder_1_out10), .out11(decoder_1_out11),
    .out12(decoder_1_out12), .out13(decoder_1_out13), .out14(decoder_1_out14), .out15(decoder_1_out15),
    .sel(Address[27:24]), .en(or_1_out));
  RAM_Block RAM0 (
    .Unsigned0_Signed1(Unsigned0_Signed1), .Reset(Reset), .Enable(decoder_1_out0), .Load(Load),
    .Store(Store), .Size_Flag(Size_Flag), .Address(Address[23:0]), .Clock(Clock), .Data_In(Data_In),
    .Data_Out(RAM0_data_out));
  RAM_Block RAM1 (
    .Unsigned0_Signed1(Unsigned0_Signed1), .Reset(Reset), .Enable(decoder_1_out1), .Load(Load),
    .Store(Store), .Size_Flag(Size_Flag), .Address(Address[23:0]), .Clock(Clock), .Data_In(Data_In),
    .Data_Out(RAM1_data_out));
  RAM_Block RAM2 (
    .Unsigned0_Signed1(Unsigned0_Signed1), .Reset(Reset), .Enable(decoder_1_out2), .Load(Load),
    .Store(Store), .Size_Flag(Size_Flag), .Address(Address[23:0]), .Clock(Clock), .Data_In(Data_In),
    .Data_Out(RAM2_data_out));
  RAM_Block RAM3 (
    .Unsigned0_Signed1(Unsigned0_Signed1), .Reset(Reset), .Enable(decoder_1_out3), .Load(Load),
    .Store(Store), .Size_Flag(Size_Flag), .Address(Address[23:0]), .Clock(Clock), .Data_In(Data_In),
    .Data_Out(RAM3_data_out));
  RAM_Block RAM4 (
    .Unsigned0_Signed1(Unsigned0_Signed1), .Reset(Reset), .Enable(decoder_1_out4), .Load(Load),
    .Store(Store), .Size_Flag(Size_Flag), .Address(Address[23:0]), .Clock(Clock), .Data_In(Data_In),
    .Data_Out(RAM4_data_out));
  RAM_Block RAM5 (
    .Unsigned0_Signed1(Unsigned0_Signed1), .Reset(Reset), .Enable(decoder_1_out5), .Load(Load),
    .Store(Store), .Size_Flag(Size_Flag), .Address(Address[23:0]), .Clock(Clock), .Data_In(Data_In),
    .Data_Out(RAM5_data_out));
  RAM_Block RAM6 (
    .Unsigned0_Signed1(Unsigned0_Signed1), .Reset(Reset), .Enable(decoder_1_out6), .Load(Load),
    .Store(Store), .Size_Flag(Size_Flag), .Address(Address[23:0]), .Clock(Clock), .Data_In(Data_In),
    .Data_Out(RAM6_data_out));
  RAM_Block RAM7 (
    .Unsigned0_Signed1(Unsigned0_Signed1), .Reset(Reset), .Enable(decoder_1_out7), .Load(Load),
    .Store(Store), .Size_Flag(Size_Flag), .Address(Address[23:0]), .Clock(Clock), .Data_In(Data_In),
    .Data_Out(RAM7_data_out));
  RAM_Block RAM8 (
    .Unsigned0_Signed1(Unsigned0_Signed1), .Reset(Reset), .Enable(decoder_1_out8), .Load(Load),
    .Store(Store), .Size_Flag(Size_Flag), .Address(Address[23:0]), .Clock(Clock), .Data_In(Data_In),
    .Data_Out(RAM8_data_out));
  RAM_Block RAM9 (
    .Unsigned0_Signed1(Unsigned0_Signed1), .Reset(Reset), .Enable(decoder_1_out9), .Load(Load),
    .Store(Store), .Size_Flag(Size_Flag), .Address(Address[23:0]), .Clock(Clock), .Data_In(Data_In),
    .Data_Out(RAM9_data_out));
  RAM_Block RAM10 (
    .Unsigned0_Signed1(Unsigned0_Signed1), .Reset(Reset), .Enable(decoder_1_out10), .Load(Load),
    .Store(Store), .Size_Flag(Size_Flag), .Address(Address[23:0]), .Clock(Clock), .Data_In(Data_In),
    .Data_Out(RAM10_data_out));
  RAM_Block RAM11 (
    .Unsigned0_Signed1(Unsigned0_Signed1), .Reset(Reset), .Enable(decoder_1_out11), .Load(Load),
    .Store(Store), .Size_Flag(Size_Flag), .Address(Address[23:0]), .Clock(Clock), .Data_In(Data_In),
    .Data_Out(RAM11_data_out));
  RAM_Block RAM12 (
    .Unsigned0_Signed1(Unsigned0_Signed1), .Reset(Reset), .Enable(decoder_1_out12), .Load(Load),
    .Store(Store), .Size_Flag(Size_Flag), .Address(Address[23:0]), .Clock(Clock), .Data_In(Data_In),
    .Data_Out(RAM12_data_out));
  RAM_Block RAM13 (
    .Unsigned0_Signed1(Unsigned0_Signed1), .Reset(Reset), .Enable(decoder_1_out13), .Load(Load),
    .Store(Store), .Size_Flag(Size_Flag), .Address(Address[23:0]), .Clock(Clock), .Data_In(Data_In),
    .Data_Out(RAM13_data_out));
  RAM_Block RAM14 (
    .Unsigned0_Signed1(Unsigned0_Signed1), .Reset(Reset), .Enable(decoder_1_out14), .Load(Load),
    .Store(Store), .Size_Flag(Size_Flag), .Address(Address[23:0]), .Clock(Clock), .Data_In(Data_In),
    .Data_Out(RAM14_data_out));
  RAM_Block RAM15 (
    .Unsigned0_Signed1(Unsigned0_Signed1), .Reset(Reset), .Enable(decoder_1_out15), .Load(Load),
    .Store(Store), .Size_Flag(Size_Flag), .Address(Address[23:0]), .Clock(Clock), .Data_In(Data_In),
    .Data_Out(RAM15_data_out));
  Multiplexer #(.enable("true"), .select(4), .width(64)) multiplexer_1 (
    .in0(RAM0_data_out), .in1(RAM1_data_out), .in2(RAM2_data_out), .in3(RAM3_data_out), .in4(RAM4_data_out),
    .in5(RAM5_data_out), .in6(RAM6_data_out), .in7(RAM7_data_out), .in8(RAM8_data_out), .in9(RAM9_data_out),
    .in10(RAM10_data_out), .in11(RAM11_data_out), .in12(RAM12_data_out), .in13(RAM13_data_out),
    .in14(RAM14_data_out), .in15(RAM15_data_out), .out(Data_Out), .sel(Address[27:24]), .en(Load));

  // Notes on the sheet:
  //   Size Flags
  //   00 = Store/Load Byte
  //   01 = Store/Load Half Word
  //   10 = Store/Load Word
  //   11 = Store/Load Long Word
  //   2^32 addresses per byte = 4GB total
  //   Implementing the entire 4GB range is unreasonable as that requires 256 RAM blocks
  //   To make this more reasonable, I'm addressing only 16 RAM blocks (4 address bits)
  //   This totals my data memory unit to 256 MB
endmodule

module RAM_Block (
  input  Unsigned0_Signed1,
  input  Reset,
  input  Enable,
  input  Load,
  input  Store,
  input  [1:0] Size_Flag,
  input  [23:0] Address,
  input  Clock,
  input  [63:0] Data_In,
  output [63:0] Data_Out
);

  wire and_1_out, and_2_out, and_3_out, and_4_out, and_5_out, or_1_out;
  wire [7:0] DMemBlock_p21, DMemBlock_p22, DMemBlock_p23, DMemBlock_p24, DMemBlock_p25, DMemBlock_p26,
       DMemBlock_p27, DMemBlock_p28, multiplexer_1_out;
  wire [63:0] bit_extender_1_out, bit_extender_2_out, bit_extender_3_out;

  and and_1 (and_1_out, Enable, Load);
  and and_2 (and_2_out, Enable, Store);
  or or_1 (or_1_out, and_1_out, and_2_out);
  Multiplexer #(.enable("true"), .select(2), .width(8)) multiplexer_1 (
    .in0(8'h1), .in1(8'h3), .in2(8'hf), .in3({8{1'b1}}), .out(multiplexer_1_out), .sel(Size_Flag),
    .en(or_1_out));
  // RAM #(.addrWidth(24), .clearpin("true"), .enables("line"), .line("octo"), .misaligned("true")) DMemBlock: pin names not known; wires that end beside it: Address, and_2_out, multiplexer_1_out[0], multiplexer_1_out[1], multiplexer_1_out[2], multiplexer_1_out[3], multiplexer_1_out[4], multiplexer_1_out[5], multiplexer_1_out[6], multiplexer_1_out[7], Clock, Data_In[7:0], Data_In[15:8], Data_In[23:16], Data_In[31:24], Data_In[39:32], Data_In[47:40], Data_In[55:48], Data_In[63:56], Reset, DMemBlock_p21, DMemBlock_p22, DMemBlock_p23, DMemBlock_p24, DMemBlock_p25, DMemBlock_p26, DMemBlock_p27, DMemBlock_p28
  and and_3 (and_3_out, Unsigned0_Signed1, DMemBlock_p21[7]);
  and and_4 (and_4_out, Unsigned0_Signed1, DMemBlock_p22[7]);
  and and_5 (and_5_out, Unsigned0_Signed1, DMemBlock_p24[7]);
  assign bit_extender_1_out = {{56{and_3_out}}, DMemBlock_p21};  // Bit_Extender bit_extender_1
  assign bit_extender_2_out = {{48{and_4_out}}, {DMemBlock_p22, DMemBlock_p21}};  // Bit_Extender bit_extender_2
  assign bit_extender_3_out = {{32{and_5_out}}, {DMemBlock_p24, DMemBlock_p23, DMemBlock_p22, DMemBlock_p21}};  // Bit_Extender bit_extender_3
  Multiplexer #(.enable("true"), .select(2), .width(64)) multiplexer_2 (
    .in0(bit_extender_1_out), .in1(bit_extender_2_out), .in2(bit_extender_3_out),
    .in3({DMemBlock_p28, DMemBlock_p27, DMemBlock_p26, DMemBlock_p25, DMemBlock_p24, DMemBlock_p23, DMemBlock_p22, DMemBlock_p21}),
    .out(Data_Out), .sel(Size_Flag), .en(and_1_out));

  // Notes on the sheet:
  //   Size Flags
  //   00 = Store/Load Byte
  //   01 = Store/Load Half Word
  //   10 = Store/Load Word
  //   11 = Store/Load Long Word
  //   This RAM Block handles up to 64 bits (8 bytes) per store or load.
  //   The Size Flag input determines whether to store/load a byte, half word, word, or long word
  //   Handles address up to 24 bits, totalling to 16 MB per RAM block
endmodule
